# Fritzing sketch CO2-Ampel (saved by Fritzing 0.9.9b)
breadboards: 1

parts:
  WeMos_D1_Mini1 = WeMos D1 Mini
  TD-er1 = MH-Z19 CO2 sensor [part_number=MH-Z19]
  Bauteil1 = 12 NeoPixel Ring [part_number=1643]
  Bauteil2 = OLED Color 1.5 inch 128x128 w microSD [part_number=1431]

nets:
  5V: WeMos_D1_Mini1.5V, TD-er1.Vin, Bauteil1.VDD, Bauteil2.3.3V
  N1: WeMos_D1_Mini1.D1, Bauteil2.SCK
  N2: WeMos_D1_Mini1.D2, Bauteil2.DC
  N3: WeMos_D1_Mini1.D3, Bauteil1.IN
  N4: WeMos_D1_Mini1.D7, TD-er1.RX
  N5: WeMos_D1_Mini1.D8, TD-er1.TX
  GND: WeMos_D1_Mini1.G, TD-er1.GND, Bauteil1.GND, Bauteil2.GND

custom parts:
  12 NeoPixel Ring: 12 ultra bright smart LED NeoPixels are arranged in a circle with 1.5" (37mm) outer diameter. The rings are 'chainable' - connect the output pin of one to the input pin of another. Use only one microcontroller pin to control as many as you can chain together! Each LED is addressable as the driver chip is inside the LED. Each one has ~18mA constant current drive so the color will be very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
  OLED Color 1.5 inch 128x128 w microSD: The visible portion of this OLED measures 1.5" diagonal and contains 128x128 RGB pixels, each one made of red, green and blue OLEDs. Each pixel can be set with 16-bits of resolution for a large range of colors. Because the display uses OLEDs, there is no backlight, and the contrast is very high (black is really black). We picked this display for its excellent color, this is the nicest mini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
